// Digital circuit CS_Project.dig as structural Verilog
module CS_Project (
  input  clk,
  output [9:0] out_2,
  output [9:0] out_3,
  output [9:0] out_4
);

  wire and_1_out, comparator_1_gt, comparator_2_eq, comparator_3_gt, L, MUXselctors2, MUXselctors3, not_1_out;
  wire [3:0] multiplexer_2_out, multiplexer_3_out;
  wire [9:0] add_1_s, Da, Db, multiplexer_1_out, MUXout1, sub_1_s;

  Multiplexer #(.Bits(10), .Selector_Bits(2)) multiplexer_1 (
    .sel(out_3[9:8]), .in_0({10{1'b0}}), .in_1({2'b00, out_3[7:0]}), .in_2(Da), .in_3(MUXout1),
    .out(multiplexer_1_out));
  Multiplexer #(.Bits(4)) multiplexer_2 (
    .sel(MUXselctors2), .in_0(out_3[3:0]), .in_1(4'b1001), .out(multiplexer_2_out));
  Comparator #(.Bits(10)) comparator_1 (.a(Da), .b(Db), .gt(comparator_1_gt));  // open: eq, lt
  Comparator #(.Bits(4)) comparator_2 (.a(multiplexer_2_out), .b(4'b0010), .eq(comparator_2_eq));  // open: gt, lt
  Multiplexer #(.Bits(4)) multiplexer_3 (
    .sel(MUXselctors3), .in_0(4'b0000), .in_1(out_3[7:4]), .out(multiplexer_3_out));
  and and_1 (and_1_out, comparator_1_gt, L);
  Register #(.Bits(10)) register_1 (.D(multiplexer_1_out), .C(clk), .en(comparator_2_eq), .Q(out_4));
  RegisterFile #(.AddrBits(4), .Bits(10)) registerfile_1 (
    .Din(multiplexer_1_out), .we(not_1_out), .Rw(multiplexer_2_out), .C(clk), .Ra(multiplexer_3_out),
    .Rb(4'b0001), .Da(Da), .Db(Db));
  not not_1 (not_1_out, L);
  CounterPreset #(.Bits(10)) counterpreset_1 (
    .en(1'b1), .C(clk), .dir(1'b0), .in({2'b00, out_3[7:0]}), .ld(and_1_out), .clr(1'b0), .out(out_2));  // open: ovf
  ROM #(.AddrBits(10), .Bits(10)) rom_1 (.A(out_2), .sel(1'b1), .D(out_3));
  Comparator #(.Bits(10)) comparator_3 (.a(out_2), .b(10'h16), .gt(comparator_3_gt));  // open: eq, lt
  Add #(.Bits(10)) add_1 (.a(Da), .b(Db), .c_i(1'b0), .s(add_1_s));  // open: c_o
  Sub #(.Bits(10)) sub_1 (.a(Da), .b(Db), .c_i(1'b0), .s(sub_1_s));  // open: c_o
  Multiplexer #(.Bits(10)) multiplexer_4 (.sel(out_3[4]), .in_0(add_1_s), .in_1(sub_1_s), .out(MUXout1));
  Decoder #(.Selector_Bits(2)) decoder_1 (
    .sel(out_3[9:8]), .out_0(L), .out_1(MUXselctors2), .out_2(MUXselctors3));  // open: out_3
  Seven_Seg seven_seg_1 (
    .a(1'b0), .b(comparator_3_gt), .c(comparator_3_gt), .d(1'b0), .e(1'b0), .f(1'b0), .g(1'b0), .dp(1'b0));

  // Other names for the same wires on the sheet: JumpAddr[7:0] = out_3[7:0]; MUXin2[3:0] = out_3[3:0];
  //   MUXin3_01[7:0] = out_3[7:0]; ALUselector = out_3[4]; MUXin1[3:0] = out_3[7:4]; _2bits[1:0] = out_3[9:8];
  //   inCounter[1:0] = out_3[9:8]

  // Notes on the sheet:
  //   clk: Hz: 5
  //   contents of rom_1 (hex, n*v repeats v):
  //   150,292,104,293,106,294,114,295,159,296,101,29e,100,29f,220,231
  //   ,312,250,221,17,2e0,2f1,e,220,241,302,220,261,e,2e0,2f1,17
endmodule
